# Fritzing sketch Alarme_arduino (saved by Fritzing 0.9.4)
breadboards: 1

parts:
  Composant1 = Arduino Mega 2560 (Rev3)
  R1 = Resistor [tolerance=±5% resistance=10k package=THT]  # not connected
  R2 = Resistor [tolerance=±5% resistance=10k package=THT]  # not connected
  R3 = Resistor [tolerance=±5% resistance=10k package=THT]  # not connected
  R4 = Resistor [tolerance=±5% resistance=10k package=THT]  # not connected
  R5 = Resistor [tolerance=±5% resistance=10k package=THT]  # not connected
  R6 = Resistor [tolerance=±5% resistance=10k package=THT]  # not connected
  R7 = Resistor [tolerance=±5% resistance=10k package=THT]  # not connected
  R8 = Resistor [tolerance=±5% resistance=10k package=THT]  # not connected
  S2 = Pushbutton [package=THT]
  S3 = Pushbutton [package=THT]
  S4 = Pushbutton [package=THT]
  S5 = Pushbutton [package=THT]
  S6 = Pushbutton [package=THT]
  S7 = Pushbutton [package=THT]
  S8 = Pushbutton [package=THT]
  S9 = Pushbutton [package=THT]
  LED1 = LED - 5mm [color="Red (633nm)" package="5 mm [THT]"]
  U1 = TLP621 [package=THT]
  R9 = Resistor [tolerance=±5% resistance=100 package=THT]
  R10 = Resistor [tolerance=±5% resistance=1.2k package=THT]
  Q1 = NPN-Transistor [package="TO92 [THT]"]
  Maluska1 = maluska dil miniaturrelais [part_number="DIL Mini RY" package=THT]
  D1 = Rectifier Diode [part_number=1N4001 package="300 mil [THT]"]
  LED2 = LED - 5mm [color="Red (633nm)" package="5 mm [THT]"]
  R11 = Resistor [tolerance=±5% resistance=220 package=THT]  # not connected

nets:
  N1: Composant1.A8, S2.leg0
  N2: Composant1.A9, S4.leg0
  N3: Composant1.A10, S5.leg0
  N4: Composant1.A11, S6.leg0
  N5: Composant1.A12, S9.leg0
  N6: Composant1.A4, LED1.cathode
  N7: Composant1.A5, S3.leg0
  N8: Composant1.A6, S7.leg0
  N9: Composant1.A7, S8.leg0
  N10: LED1.anode, U1.Pin_1
  N11: U1.Pin_2, R9.Pin_1
  5V: U1.Pin_4, R9.Pin_0
  N12: U1.Pin_3, R10.Pin_1
  N13: R10.Pin_0, Q1.B
  N14: Q1.C, Maluska1.1, D1.anode
  12V: Maluska1.9, Maluska1.11, D1.cathode
  N15: Maluska1.13, LED2.anode

notes:
  SCHEMA CABLAGE ALARME ARDUINO
